# Fritzing sketch arduino (saved by Fritzing 0.9.3b)
breadboards: 1

parts:
  Part1 = Arduino Uno (Rev3) - ICSP
  BT1 = Bluetooth HC-06d [package=THT]
  HC-SR04_Sensor_1 = HC-SR04 Ultrasonic Distance Sensor
  J3 = Basic Servo
  J4 = Basic Servo
  R1 = Resistor [tolerance=±5% resistance=220 package=THT]
  R2 = Resistor [tolerance=±5% resistance=220 package=THT]
  R4 = Resistor [tolerance=±5% resistance=220 package=THT]
  R5 = Resistor [tolerance=±5% resistance=220 package=THT]
  R6 = Resistor [tolerance=±5% resistance=220 package=THT]
  R7 = Resistor [tolerance=±5% resistance=220 package=THT]
  R8 = Resistor [tolerance=±5% resistance=220 package=THT]
  LED1 = LED - 5mm [color="Red (633nm)" package="5 mm [THT]"]
  LED2 = LED - 5mm [color="Red (633nm)" package="5 mm [THT]"]
  LED4 = LED - 5mm [color="Red (633nm)" package="5 mm [THT]"]
  LED5 = LED - 5mm [color="Red (633nm)" package="5 mm [THT]"]
  LED6 = LED - 5mm [color="Red (633nm)" package="5 mm [THT]"]
  LED7 = LED - 5mm [color="Red (633nm)" package="5 mm [THT]"]
  LED8 = LED - 5mm [color="Red (633nm)" package="5 mm [THT]"]
  Grove_Buzzer1 = Grove Buzzer

nets:
  N1: Part1.ICSP_MISO, Part1.D12/MISO, R2.Pin_0
  N2: Part1.D8, Grove_Buzzer1.SIG
  N3: Part1.D10_PWM/SS, J4.pulse
  N4: Part1.D11_PWM/MOSI, J3.pulse
  N5: Part1.D13/SCK, R1.Pin_0
  N6: Part1.D0/RX, BT1.TXD
  N7: Part1.D1/TX, BT1.RXD
  N8: Part1.D2, HC-SR04_Sensor_1.ECHO
  N9: Part1.D3_PWM, HC-SR04_Sensor_1.TRIG
  N10: Part1.D4, R7.Pin_0, R8.Pin_0
  N11: Part1.D5_PWM, R6.Pin_0
  N12: Part1.D6_PWM, R5.Pin_0
  N13: Part1.D7, R4.Pin_0
  3V3: Part1.3V3, BT1.VCC
  VCC: Part1.5V, HC-SR04_Sensor_1.VCC, J3.vcc, J4.vcc, Grove_Buzzer1.VCC
  GND: Part1.GND, BT1.GND, HC-SR04_Sensor_1.GND, J3.gnd, J4.gnd, LED1.cathode, LED2.cathode, LED4.cathode, LED5.cathode, LED6.cathode, LED7.cathode, LED8.cathode, Grove_Buzzer1.GND
  N14: R1.Pin_1, LED1.anode
  N15: R2.Pin_1, LED2.anode
  N16: R4.Pin_1, LED4.anode
  N17: R5.Pin_1, LED5.anode
  N18: R6.Pin_1, LED6.anode
  N19: R7.Pin_1, LED7.anode
  N20: R8.Pin_1, LED8.anode

custom parts:
  Bluetooth HC-06d: Bluetooth HC-06 - face down, pins down 16.5mm x 37.5mm PCB
  Grove Buzzer: Buzzer, Grove connector.
